// Logisim project CPU_p3.circ as structural Verilog: 11 circuits, main circuit main
module main (
  input  rst,
  output [31:0] Instr,
  output [31:0] pc,
  output RegWrite,
  output [4:0] RegAddr,
  output [31:0] RegData,
  output MemWrite,
  output [31:0] MemAddr,
  output [31:0] MemData
);

  wire bj_1_branch_taken, BJ_EN_ctrl, BJ_INV_ctrl, clk, multiplexer_5_out;
  wire [1:0] ALU_IN1_ctrl, ALU_IN2_ctrl, DM_DS_ctrl, DM_LU_ctrl, EXT_OP_ctrl, GRF_WA_ctrl, GRF_WD_ctrl,
       NPC_OP_ctrl;
  wire [3:0] ALU_OP_ctrl;
  wire [31:0] dm_1_read_data, ext_1_output, grf_1_read_data1, multiplexer_3_out, multiplexer_4_out,
       npc_1_next_pc;

  Clock clock_1 (.out(clk));
  IFU ifu_1 (.clk(clk), .rst(rst), .next_pc(npc_1_next_pc), .pc(pc), .instruction(Instr));
  CTRL ctrl_1 (
    .instruction(Instr), .NPC_OP(NPC_OP_ctrl), .BJ_EN(BJ_EN_ctrl), .BJ_INV(BJ_INV_ctrl), .GRF_WEN(RegWrite),
    .GRF_WA(GRF_WA_ctrl), .GRF_WD(GRF_WD_ctrl), .EXT_OP(EXT_OP_ctrl), .ALU_OP(ALU_OP_ctrl),
    .ALU_IN1(ALU_IN1_ctrl), .DM_WEN(MemWrite), .ALU_IN2(ALU_IN2_ctrl), .DM_DS(DM_DS_ctrl), .DM_LU(DM_LU_ctrl));
  NPC npc_1 (
    .pc(pc), .instruction(Instr), .branch_taken(bj_1_branch_taken), .op_control(NPC_OP_ctrl),
    .next_pc(npc_1_next_pc));  // open: reg_target, pc_plus4
  EXT ext_1 (.\input (Instr[15:0]), .op_control(EXT_OP_ctrl), .\output (ext_1_output));
  Multiplexer #(.select(2), .width(5), .enable("false")) multiplexer_1 (
    .in0(Instr[20:16]), .in1(Instr[15:11]), .out(RegAddr), .sel(GRF_WA_ctrl));  // open: in2, in3
  Multiplexer #(.select(2), .width(32), .enable("false")) multiplexer_2 (
    .in0(ext_1_output), .in1(MemAddr), .in2(dm_1_read_data), .out(RegData), .sel(GRF_WD_ctrl));  // open: in3
  GRF grf_1 (
    .read_addr1(Instr[25:21]), .read_addr2(Instr[20:16]), .write_addr(RegAddr), .write_data(RegData),
    .write_enable(RegWrite), .clk(clk), .rst(rst), .read_data1(grf_1_read_data1), .read_data2(MemData));
  Multiplexer #(.select(2), .width(32), .enable("false")) multiplexer_3 (
    .in0(grf_1_read_data1), .out(multiplexer_3_out), .sel(ALU_IN1_ctrl));  // open: in1, in2, in3
  ALU alu_1 (.input1(multiplexer_3_out), .input2(multiplexer_4_out), .op_control(ALU_OP_ctrl), .\output (MemAddr));
  Multiplexer #(.select(2), .width(32), .enable("false")) multiplexer_4 (
    .in0(MemData), .in1(ext_1_output), .out(multiplexer_4_out), .sel(ALU_IN2_ctrl));  // open: in2, in3
  Multiplexer #(.select(2), .enable("false")) multiplexer_5 (
    .in0(1'b0), .in1(1'b1), .out(multiplexer_5_out), .sel(DM_LU_ctrl));  // open: in2, in3
  BJ bj_1 (
    .cmp_result(MemAddr[0]), .branch_enable(BJ_EN_ctrl), .branch_invert(BJ_INV_ctrl),
    .branch_taken(bj_1_branch_taken));
  DM dm_1 (
    .addr(MemAddr), .write_data(MemData), .write_enable(MemWrite), .clk(clk), .rst(rst),
    .read_data(dm_1_read_data), .data_size(DM_DS_ctrl), .load_unsigned(multiplexer_5_out));

  // Other names for the same wires on the sheet: DM_WEN_ctrl = MemWrite; GRF_WEN_ctrl = RegWrite; MA[31:0] = MemAddr;
  //   MD[31:0] = MemData; RA[4:0] = RegAddr; RD[31:0] = RegData
endmodule

module IFU (
  input  clk,
  input  rst,
  input  [31:0] next_pc,
  output [31:0] pc,
  output [31:0] instruction
);

  wire [31:0] register_1_q, subtractor_1_out, xor_1_out;

  assign xor_1_out = 32'h3000 ^ next_pc;  // XOR_Gate xor_1, 32 bits wide
  Register #(.width(32)) register_1 (.D(xor_1_out), .Q(register_1_q), .clk(clk), .clr(rst));  // open: en
  assign pc = 32'h3000 ^ register_1_q;  // XOR_Gate xor_2, 32 bits wide
  Subtractor #(.width(32)) subtractor_1 (.a(pc), .b(32'h3000), .out(subtractor_1_out));  // open: bin, bout
  ROM #(.addrWidth(12), .dataWidth(32)) rom_1 (.addr(subtractor_1_out[13:2]), .data(instruction));  // open: sel

  // Other names for the same wires on the sheet: INS[31:0] = instruction; NPC[31:0] = next_pc
endmodule

module ALU (
  input  [31:0] input1,
  input  [31:0] input2,
  input  [3:0] op_control,
  output [31:0] \output 
);

  wire comparator_1_eq, comparator_1_gt, comparator_1_lt, comparator_2_gt, comparator_2_lt;
  wire [31:0] adder_1_out, bit_extender_1_out, bit_extender_2_out, bit_extender_3_out, bit_extender_4_out,
       bit_extender_5_out, or_1_out, subtractor_1_out;

  Adder #(.width(32)) adder_1 (.a(input1), .b(input2), .out(adder_1_out));  // open: cin, cout
  Subtractor #(.width(32)) subtractor_1 (.a(input1), .b(input2), .out(subtractor_1_out));  // open: bin, bout
  assign or_1_out = input1 | input2;  // OR_Gate or_1, 32 bits wide
  Comparator #(.width(32)) comparator_1 (
    .a(input1), .b(input2), .gt(comparator_1_gt), .eq(comparator_1_eq), .lt(comparator_1_lt));
  Comparator #(.width(32), .mode("unsigned")) comparator_2 (
    .a(input1), .b(input2), .gt(comparator_2_gt), .lt(comparator_2_lt));  // open: eq
  assign bit_extender_1_out = {{31{1'b0}}, comparator_1_gt};  // Bit_Extender bit_extender_1
  assign bit_extender_2_out = {{31{1'b0}}, comparator_2_gt};  // Bit_Extender bit_extender_2
  assign bit_extender_3_out = {{31{1'b0}}, comparator_1_eq};  // Bit_Extender bit_extender_3
  assign bit_extender_4_out = {{31{1'b0}}, comparator_1_lt};  // Bit_Extender bit_extender_4
  assign bit_extender_5_out = {{31{1'b0}}, comparator_2_lt};  // Bit_Extender bit_extender_5
  Multiplexer #(.select(4), .width(32), .enable("false")) multiplexer_1 (
    .in0(adder_1_out), .in1(subtractor_1_out), .in2(or_1_out), .in3(bit_extender_3_out),
    .in4(bit_extender_1_out), .in5(bit_extender_4_out), .in6(bit_extender_2_out), .in7(bit_extender_5_out),
    .out(\output ), .sel(op_control));  // open: in8, in9, in10, in11, in12, in13, in14, in15

  // Other names for the same wires on the sheet: CTRL[3:0] = op_control; IN1[31:0] = input1; IN2[31:0] = input2;
  //   OUT[31:0] = \output 
endmodule

module BJ (
  input  cmp_result,
  input  branch_enable,
  input  branch_invert,
  output branch_taken
);

  wire xor_1_out;

  xor xor_1 (xor_1_out, cmp_result, branch_invert);
  and and_1 (branch_taken, xor_1_out, branch_enable);

  // Other names for the same wires on the sheet: BE = branch_enable; BI = branch_invert; BT = branch_taken;
  //   CMP = cmp_result
endmodule

module NPC (
  input  [31:0] pc,
  input  [31:0] instruction,
  input  [31:0] reg_target,
  input  branch_taken,
  input  [1:0] op_control,
  output [31:0] next_pc,
  output [31:0] pc_plus4
);

  wire [31:0] adder_2_out, bit_extender_1_out, multiplexer_1_out, shifter_1_out;

  Adder #(.width(32)) adder_1 (.a(32'h4), .b(pc), .out(pc_plus4));  // open: cin, cout
  assign bit_extender_1_out = {{16{instruction[15]}}, instruction[15:0]};  // Bit_Extender bit_extender_1
  Shifter #(.width(32)) shifter_1 (.in(bit_extender_1_out), .\dist (5'b00010), .out(shifter_1_out));
  Adder #(.width(32)) adder_2 (.a(pc_plus4), .b(shifter_1_out), .out(adder_2_out));  // open: cin, cout
  Multiplexer #(.width(32), .enable("false")) multiplexer_1 (
    .in0(pc_plus4), .in1(adder_2_out), .out(multiplexer_1_out), .sel(branch_taken));
  Multiplexer #(.select(2), .width(32), .enable("false")) multiplexer_2 (
    .in0(pc_plus4), .in1(multiplexer_1_out), .out(next_pc), .sel(op_control));  // open: in2, in3

  // Other names for the same wires on the sheet: BT = branch_taken; CTRL[1:0] = op_control; INS[31:0] = instruction;
  //   NPC[31:0] = next_pc; PP4[31:0] = pc_plus4; RT[31:0] = reg_target
endmodule

module CTRL (
  input  [31:0] instruction,
  output [1:0] NPC_OP,
  output BJ_EN,
  output BJ_INV,
  output GRF_WEN,
  output [1:0] GRF_WA,
  output [1:0] GRF_WD,
  output [1:0] EXT_OP,
  output [3:0] ALU_OP,
  output [1:0] ALU_IN1,
  output [1:0] ALU_IN2,
  output DM_WEN,
  output [1:0] DM_DS,
  output [1:0] DM_LU
);

  wire add, beq, comparator_6_eq, comparator_7_eq, comparator_8_eq, lui, lw, ori, sub, sw;
  wire [3:0] priority_encoder_1_out;

  Comparator #(.width(6)) comparator_1 (.a(6'b001111), .b(instruction[31:26]), .eq(lui));  // open: gt, lt
  Comparator #(.width(6)) comparator_2 (.a(6'b000100), .b(instruction[31:26]), .eq(beq));  // open: gt, lt
  Comparator #(.width(6)) comparator_3 (.a(6'b101011), .b(instruction[31:26]), .eq(sw));  // open: gt, lt
  Comparator #(.width(6)) comparator_4 (.a(6'b100011), .b(instruction[31:26]), .eq(lw));  // open: gt, lt
  Comparator #(.width(6)) comparator_5 (.a(6'b001101), .b(instruction[31:26]), .eq(ori));  // open: gt, lt
  Comparator #(.width(6)) comparator_6 (.a({6{1'b0}}), .b(instruction[31:26]), .eq(comparator_6_eq));  // open: gt, lt
  Comparator #(.width(6)) comparator_7 (.a(6'b100010), .b(instruction[5:0]), .eq(comparator_7_eq));  // open: gt, lt
  Comparator #(.width(6)) comparator_8 (.a(6'b100000), .b(instruction[5:0]), .eq(comparator_8_eq));  // open: gt, lt
  and and_1 (sub, comparator_7_eq, comparator_6_eq);
  and and_2 (add, comparator_8_eq, comparator_6_eq);
  Priority_Encoder #(.select(4)) priority_encoder_1 (
    .in0(1'b1), .in1(add), .in2(sub), .in3(ori), .in4(lw), .in5(sw), .in6(beq), .in7(lui),
    .out(priority_encoder_1_out));  // open: in8, in9, in10, in11, in12, in13, in14, in15, gs, en_out, en_in
  Multiplexer #(.select(4), .enable("false")) multiplexer_1 (
    .in0(1'b0), .in1(1'b0), .in2(1'b0), .in3(1'b0), .in4(1'b0), .in5(1'b1), .in6(1'b0), .in7(1'b0),
    .out(DM_WEN), .sel(priority_encoder_1_out));  // open: in8, in9, in10, in11, in12, in13, in14, in15
  Multiplexer #(.select(4), .width(2), .enable("false")) multiplexer_2 (
    .in0(2'b00), .in1(2'b01), .in2(2'b01), .in3(2'b01), .in4(2'b10), .in5(2'b00), .in6(2'b00), .in7(2'b00),
    .out(GRF_WD), .sel(priority_encoder_1_out));  // open: in8, in9, in10, in11, in12, in13, in14, in15
  Multiplexer #(.select(4), .width(2), .enable("false")) multiplexer_3 (
    .in0(2'b00), .in1(2'b00), .in2(2'b00), .in3(2'b00), .in4(2'b00), .in5(2'b00), .in6(2'b01), .in7(2'b00),
    .out(NPC_OP), .sel(priority_encoder_1_out));  // open: in8, in9, in10, in11, in12, in13, in14, in15
  Multiplexer #(.select(4), .width(2), .enable("false")) multiplexer_4 (
    .in0(2'b00), .in1(2'b00), .in2(2'b00), .in3(2'b00), .in4(2'b00), .in5(2'b00), .in6(2'b00), .in7(2'b00),
    .out(DM_DS), .sel(priority_encoder_1_out));  // open: in8, in9, in10, in11, in12, in13, in14, in15
  Multiplexer #(.select(4), .width(2), .enable("false")) multiplexer_5 (
    .in0(2'b00), .in1(2'b00), .in2(2'b00), .in3(2'b01), .in4(2'b00), .in5(2'b00), .in6(2'b00), .in7(2'b10),
    .out(EXT_OP), .sel(priority_encoder_1_out));  // open: in8, in9, in10, in11, in12, in13, in14, in15
  Multiplexer #(.select(4), .enable("false")) multiplexer_6 (
    .in0(1'b0), .in1(1'b0), .in2(1'b0), .in3(1'b0), .in4(1'b0), .in5(1'b0), .in6(1'b1), .in7(1'b0),
    .out(BJ_EN), .sel(priority_encoder_1_out));  // open: in8, in9, in10, in11, in12, in13, in14, in15
  Multiplexer #(.select(4), .width(2), .enable("false")) multiplexer_7 (
    .in0(2'b00), .in1(2'b00), .in2(2'b00), .in3(2'b00), .in4(2'b00), .in5(2'b00), .in6(2'b00), .in7(2'b00),
    .out(DM_LU), .sel(priority_encoder_1_out));  // open: in8, in9, in10, in11, in12, in13, in14, in15
  Multiplexer #(.select(4), .width(4), .enable("false")) multiplexer_8 (
    .in0(4'b0000), .in1(4'b0000), .in2(4'b0001), .in3(4'b0010), .in4(4'b0000), .in5(4'b0000), .in6(4'b0011),
    .in7(4'b0000), .out(ALU_OP), .sel(priority_encoder_1_out));  // open: in8, in9, in10, in11, in12, in13, in14, in15
  Multiplexer #(.select(4), .enable("false")) multiplexer_9 (
    .in0(1'b0), .in1(1'b0), .in2(1'b0), .in3(1'b0), .in4(1'b0), .in5(1'b0), .in6(1'b0), .in7(1'b0),
    .out(BJ_INV), .sel(priority_encoder_1_out));  // open: in8, in9, in10, in11, in12, in13, in14, in15
  Multiplexer #(.select(4), .width(2), .enable("false")) multiplexer_10 (
    .in0(2'b00), .in1(2'b00), .in2(2'b00), .in3(2'b00), .in4(2'b00), .in5(2'b00), .in6(2'b00), .in7(2'b00),
    .out(ALU_IN1), .sel(priority_encoder_1_out));  // open: in8, in9, in10, in11, in12, in13, in14, in15
  Multiplexer #(.select(4), .enable("false")) multiplexer_11 (
    .in0(1'b0), .in1(1'b1), .in2(1'b1), .in3(1'b1), .in4(1'b1), .in5(1'b0), .in6(1'b0), .in7(1'b1),
    .out(GRF_WEN), .sel(priority_encoder_1_out));  // open: in8, in9, in10, in11, in12, in13, in14, in15
  Multiplexer #(.select(4), .width(2), .enable("false")) multiplexer_12 (
    .in0(2'b00), .in1(2'b00), .in2(2'b00), .in3(2'b01), .in4(2'b01), .in5(2'b01), .in6(2'b00), .in7(2'b00),
    .out(ALU_IN2), .sel(priority_encoder_1_out));  // open: in8, in9, in10, in11, in12, in13, in14, in15
  Multiplexer #(.select(4), .width(2), .enable("false")) multiplexer_13 (
    .in0(2'b00), .in1(2'b01), .in2(2'b01), .in3(2'b00), .in4(2'b00), .in5(2'b00), .in6(2'b00), .in7(2'b00),
    .out(GRF_WA), .sel(priority_encoder_1_out));  // open: in8, in9, in10, in11, in12, in13, in14, in15

  // Other names for the same wires on the sheet: INS[31:0] = instruction
endmodule

module EXT (
  input  [15:0] \input ,
  input  [1:0] op_control,
  output [31:0] \output 
);

  wire [31:0] bit_extender_1_out, bit_extender_2_out;

  assign bit_extender_1_out = {{16{\input [15]}}, \input };  // Bit_Extender bit_extender_1
  assign bit_extender_2_out = {{16{1'b0}}, \input };  // Bit_Extender bit_extender_2
  Multiplexer #(.select(2), .width(32), .enable("false")) multiplexer_1 (
    .in0(bit_extender_1_out), .in1(bit_extender_2_out), .in2({\input , {16{1'b0}}}), .out(\output ),
    .sel(op_control));  // open: in3

  // Other names for the same wires on the sheet: IN[15:0] = \input ; CTRL[1:0] = op_control; OUT[31:0] = \output 
endmodule

module GRF (
  input  [4:0] read_addr1,
  input  [4:0] read_addr2,
  input  [4:0] write_addr,
  input  [31:0] write_data,
  input  write_enable,
  input  clk,
  input  rst,
  output [31:0] read_data1,
  output [31:0] read_data2
);

  wire Wen1, Wen2, Wen3, Wen4, Wen5, Wen6, Wen7, Wen8, Wen9, Wen10, Wen11, Wen12, Wen13, Wen14, Wen15, Wen16,
       Wen17, Wen18, Wen19, Wen20, Wen21, Wen22, Wen23, Wen24, Wen25, Wen26, Wen27, Wen28, Wen29, Wen30,
       Wen31;
  wire [31:0] Q0, Q1, Q2, Q3, Q4, Q5, Q6, Q7, Q8, Q9, Q10, Q11, Q12, Q13, Q14, Q15, Q16, Q17, Q18, Q19, Q20,
       Q21, Q22, Q23, Q24, Q25, Q26, Q27, Q28, Q29, Q30, Q31;

  Register #(.width(32)) _0 (.D(write_data), .en(1'b0), .Q(Q0), .clk(clk), .clr(rst));
  Register #(.width(32)) _8 (.D(write_data), .en(Wen8), .Q(Q8), .clk(clk), .clr(rst));
  Register #(.width(32)) _16 (.D(write_data), .en(Wen16), .Q(Q16), .clk(clk), .clr(rst));
  Register #(.width(32)) _24 (.D(write_data), .en(Wen24), .Q(Q24), .clk(clk), .clr(rst));
  Register #(.width(32)) _1 (.D(write_data), .en(Wen1), .Q(Q1), .clk(clk), .clr(rst));
  Register #(.width(32)) _9 (.D(write_data), .en(Wen9), .Q(Q9), .clk(clk), .clr(rst));
  Register #(.width(32)) _17 (.D(write_data), .en(Wen17), .Q(Q17), .clk(clk), .clr(rst));
  Register #(.width(32)) _25 (.D(write_data), .en(Wen25), .Q(Q25), .clk(clk), .clr(rst));
  Register #(.width(32)) _2 (.D(write_data), .en(Wen2), .Q(Q2), .clk(clk), .clr(rst));
  Register #(.width(32)) _10 (.D(write_data), .en(Wen10), .Q(Q10), .clk(clk), .clr(rst));
  Register #(.width(32)) _18 (.D(write_data), .en(Wen18), .Q(Q18), .clk(clk), .clr(rst));
  Register #(.width(32)) _26 (.D(write_data), .en(Wen26), .Q(Q26), .clk(clk), .clr(rst));
  Register #(.width(32)) _3 (.D(write_data), .en(Wen3), .Q(Q3), .clk(clk), .clr(rst));
  Register #(.width(32)) _11 (.D(write_data), .en(Wen11), .Q(Q11), .clk(clk), .clr(rst));
  Register #(.width(32)) _19 (.D(write_data), .en(Wen19), .Q(Q19), .clk(clk), .clr(rst));
  Register #(.width(32)) _27 (.D(write_data), .en(Wen27), .Q(Q27), .clk(clk), .clr(rst));
  Multiplexer #(.select(5), .width(32), .enable("false")) multiplexer_1 (
    .in0(Q0), .in1(Q1), .in2(Q2), .in3(Q3), .in4(Q4), .in5(Q5), .in6(Q6), .in7(Q7), .in8(Q8), .in9(Q9),
    .in10(Q10), .in11(Q11), .in12(Q12), .in13(Q13), .in14(Q14), .in15(Q15), .in16(Q16), .in17(Q17),
    .in18(Q18), .in19(Q19), .in20(Q20), .in21(Q21), .in22(Q22), .in23(Q23), .in24(Q24), .in25(Q25),
    .in26(Q26), .in27(Q27), .in28(Q28), .in29(Q29), .in30(Q30), .in31(Q31), .out(read_data1), .sel(read_addr1));
  Register #(.width(32)) _4 (.D(write_data), .en(Wen4), .Q(Q4), .clk(clk), .clr(rst));
  Register #(.width(32)) _12 (.D(write_data), .en(Wen12), .Q(Q12), .clk(clk), .clr(rst));
  Register #(.width(32)) _20 (.D(write_data), .en(Wen20), .Q(Q20), .clk(clk), .clr(rst));
  Register #(.width(32)) _28 (.D(write_data), .en(Wen28), .Q(Q28), .clk(clk), .clr(rst));
  Multiplexer #(.select(5), .width(32), .enable("false")) multiplexer_2 (
    .in0(Q0), .in1(Q1), .in2(Q2), .in3(Q3), .in4(Q4), .in5(Q5), .in6(Q6), .in7(Q7), .in8(Q8), .in9(Q9),
    .in10(Q10), .in11(Q11), .in12(Q12), .in13(Q13), .in14(Q14), .in15(Q15), .in16(Q16), .in17(Q17),
    .in18(Q18), .in19(Q19), .in20(Q20), .in21(Q21), .in22(Q22), .in23(Q23), .in24(Q24), .in25(Q25),
    .in26(Q26), .in27(Q27), .in28(Q28), .in29(Q29), .in30(Q30), .in31(Q31), .out(read_data2), .sel(read_addr2));
  Register #(.width(32)) _5 (.D(write_data), .en(Wen5), .Q(Q5), .clk(clk), .clr(rst));
  Register #(.width(32)) _13 (.D(write_data), .en(Wen13), .Q(Q13), .clk(clk), .clr(rst));
  Register #(.width(32)) _21 (.D(write_data), .en(Wen21), .Q(Q21), .clk(clk), .clr(rst));
  Register #(.width(32)) _29 (.D(write_data), .en(Wen29), .Q(Q29), .clk(clk), .clr(rst));
  Register #(.width(32)) _6 (.D(write_data), .en(Wen6), .Q(Q6), .clk(clk), .clr(rst));
  Register #(.width(32)) _14 (.D(write_data), .en(Wen14), .Q(Q14), .clk(clk), .clr(rst));
  Register #(.width(32)) _22 (.D(write_data), .en(Wen22), .Q(Q22), .clk(clk), .clr(rst));
  Register #(.width(32)) _30 (.D(write_data), .en(Wen30), .Q(Q30), .clk(clk), .clr(rst));
  Register #(.width(32)) _7 (.D(write_data), .en(Wen7), .Q(Q7), .clk(clk), .clr(rst));
  Register #(.width(32)) _15 (.D(write_data), .en(Wen15), .Q(Q15), .clk(clk), .clr(rst));
  Register #(.width(32)) _23 (.D(write_data), .en(Wen23), .Q(Q23), .clk(clk), .clr(rst));
  Register #(.width(32)) _31 (.D(write_data), .en(Wen31), .Q(Q31), .clk(clk), .clr(rst));
  Demultiplexer #(.select(5), .enable("false")) demultiplexer_1 (
    .out1(Wen1), .out2(Wen2), .out3(Wen3), .out4(Wen4), .out5(Wen5), .out6(Wen6), .out7(Wen7), .out8(Wen8),
    .out9(Wen9), .out10(Wen10), .out11(Wen11), .out12(Wen12), .out13(Wen13), .out14(Wen14), .out15(Wen15),
    .out16(Wen16), .out17(Wen17), .out18(Wen18), .out19(Wen19), .out20(Wen20), .out21(Wen21), .out22(Wen22),
    .out23(Wen23), .out24(Wen24), .out25(Wen25), .out26(Wen26), .out27(Wen27), .out28(Wen28), .out29(Wen29),
    .out30(Wen30), .out31(Wen31), .in(write_enable), .sel(write_addr));  // open: out0

  // Other names for the same wires on the sheet: RA1[4:0] = read_addr1; RA2[4:0] = read_addr2; RD1[31:0] = read_data1;
  //   RD2[31:0] = read_data2; WA[4:0] = write_addr; WD[31:0] = write_data; Wen = write_enable
endmodule

module DM (
  input  [31:0] addr,
  input  [31:0] write_data,
  input  [1:0] data_size,
  input  load_unsigned,
  input  write_enable,
  input  clk,
  input  rst,
  output [31:0] read_data
);

  wire [31:0] ram_1_data, sm_1_new_word;

  SM sm_1 (
    .old_word(ram_1_data), .write_data(write_data), .data_size(data_size), .byte_offset(addr[1:0]),
    .new_word(sm_1_new_word));
  RAM #(.addrWidth(12), .dataWidth(32), .bus("separate")) ram_1 (
    .addr(addr[13:2]), .din(sm_1_new_word), .data(ram_1_data), .str(write_enable), .sel(1'b1), .clk(clk),
    .ld(1'b1), .clr(rst));
  LE le_1 (
    .word_data(ram_1_data), .data_size(data_size), .byte_offset(addr[1:0]), .load_unsigned(load_unsigned),
    .read_data(read_data));

  // Other names for the same wires on the sheet: DS[1:0] = data_size; LU = load_unsigned; RD[31:0] = read_data;
  //   WD[31:0] = write_data; WEN = write_enable
endmodule

module SM (
  input  [31:0] old_word,
  input  [31:0] write_data,
  input  [1:0] data_size,
  input  [1:0] byte_offset,
  output [31:0] new_word
);

  wire [31:0] multiplexer_1_out, multiplexer_2_out;

  Multiplexer #(.width(32), .enable("false")) multiplexer_1 (
    .in0({old_word[31:16], write_data[15:0]}), .in1({write_data[15:0], old_word[15:0]}),
    .out(multiplexer_1_out), .sel(byte_offset[1]));
  Multiplexer #(.select(2), .width(32), .enable("false")) multiplexer_2 (
    .in0({old_word[31:8], write_data[7:0]}), .in1({old_word[31:16], write_data[7:0], old_word[7:0]}),
    .in2({old_word[31:24], write_data[7:0], old_word[15:0]}), .in3({write_data[7:0], old_word[23:0]}),
    .out(multiplexer_2_out), .sel(byte_offset));
  Multiplexer #(.select(2), .width(32), .enable("false")) multiplexer_3 (
    .in0(write_data), .in1(multiplexer_1_out), .in2(multiplexer_2_out), .out(new_word), .sel(data_size));  // open: in3

  // Other names for the same wires on the sheet: WD[31:0] = write_data; OW[31:0] = old_word; BO[1:0] = byte_offset;
  //   DS[1:0] = data_size; NW[31:0] = new_word
endmodule

module LE (
  input  [31:0] word_data,
  input  [1:0] data_size,
  input  [1:0] byte_offset,
  input  load_unsigned,
  output [31:0] read_data
);

  wire [7:0] multiplexer_2_out;
  wire [15:0] multiplexer_1_out;
  wire [31:0] bit_extender_1_out, bit_extender_2_out, bit_extender_3_out, bit_extender_4_out,
       multiplexer_3_out, multiplexer_4_out;

  Multiplexer #(.width(16), .enable("false")) multiplexer_1 (
    .in0(word_data[15:0]), .in1(word_data[31:16]), .out(multiplexer_1_out), .sel(byte_offset[1]));
  Multiplexer #(.select(2), .width(8), .enable("false")) multiplexer_2 (
    .in0(word_data[7:0]), .in1(word_data[15:8]), .in2(word_data[23:16]), .in3(word_data[31:24]),
    .out(multiplexer_2_out), .sel(byte_offset));
  assign bit_extender_1_out = {{16{multiplexer_1_out[15]}}, multiplexer_1_out};  // Bit_Extender bit_extender_1
  assign bit_extender_2_out = {{16{1'b0}}, multiplexer_1_out};  // Bit_Extender bit_extender_2
  assign bit_extender_3_out = {{24{multiplexer_2_out[7]}}, multiplexer_2_out};  // Bit_Extender bit_extender_3
  assign bit_extender_4_out = {{24{1'b0}}, multiplexer_2_out};  // Bit_Extender bit_extender_4
  Multiplexer #(.width(32), .enable("false")) multiplexer_3 (
    .in0(bit_extender_1_out), .in1(bit_extender_2_out), .out(multiplexer_3_out), .sel(load_unsigned));
  Multiplexer #(.width(32), .enable("false")) multiplexer_4 (
    .in0(bit_extender_3_out), .in1(bit_extender_4_out), .out(multiplexer_4_out), .sel(load_unsigned));
  Multiplexer #(.select(2), .width(32), .enable("false")) multiplexer_5 (
    .in0(word_data), .in1(multiplexer_3_out), .in2(multiplexer_4_out), .out(read_data), .sel(data_size));  // open: in3

  // Other names for the same wires on the sheet: BO[1:0] = byte_offset; DS[1:0] = data_size; LU = load_unsigned;
  //   RD[31:0] = read_data; WD[31:0] = word_data
endmodule
